# Fritzing sketch electronic scheme (saved by Fritzing 1.0.0rc)

parts:
  DRV_1 = DRV 8825 Stepper Motor Carrier, High Current [part_number="DRV 8825"]
  DRV_2 = DRV 8825 Stepper Motor Carrier, High Current [part_number="DRV 8825"]
  M1 = Stepper Motor - Bipolar
  M2 = Stepper Motor - Bipolar
  V1 = DC Power [voltage=12V frequency=60]
  Part1 = Arduino Uno (Rev3) - ICSP
  Part2 = HX711 Weighing Sensor Module
  V2 = DC Power [voltage=12V frequency=60]
  DC_FAN = DC Motor [voltage_(max)=12V voltage_(min)=3V]
  V3 = DC Power [voltage=12V frequency=60]
  LCD1 = LCD screen
  LCM1602_IIC1 = LCM1602 IIC [part_number="LCM1602 IIC" chip_label="LCM1602 IIC" package="DIP (Dual Inline) [THT]"]
  S1 = Pushbutton [package="[THT]"]
  S2 = Pushbutton [package="[THT]"]
  RESET = Pushbutton [package="[THT]"]

nets:
  N1: DRV_1.ENABLE, Part1.D8
  N2: DRV_1.STEP, Part1.D6_PWM
  N3: DRV_1.DIRECTION, Part1.D7
  N4: DRV_1.VOLTAGE_ST/_MT, DRV_2.VOLTAGE_ST/_MT, V1.V+
  N5: DRV_1.GROUND_ST/_MT, DRV_2.GROUND_ST/_MT, V1.V-
  N6: DRV_1.OUT_2B, M2.A
  N7: DRV_1.OUT_2A, M2.C
  N8: DRV_1.OUT_1A, M2.B
  N9: DRV_1.OUT_1B, M2.D
  N10: DRV_1.VOLTAGE_DD, DRV_2.VOLTAGE_DD, Part1.5V
  GND: DRV_1.GROUND_LOG, DRV_2.GROUND_LOG, Part1.GND, V2.V-, LCM1602_IIC1.GND, S1.Pin_3, S1.Pin_4, S2.Pin_3, S2.Pin_4, RESET.Pin_3
  N11: DRV_2.ENABLE, Part1.D12/MISO
  N12: DRV_2.STEP, Part1.D5_PWM
  N13: DRV_2.DIRECTION, Part1.D4
  N14: DRV_2.OUT_2B, M1.A
  N15: DRV_2.OUT_2A, M1.C
  N16: DRV_2.OUT_1A, M1.B
  N17: DRV_2.OUT_1B, M1.D
  N18: Part1.ICSP_MOSI, Part1.D11_PWM/MOSI, Part2.DO/RX
  N19: Part1.D13/SCK, Part2.CK/TX
  N20: Part1.A4/SDA, LCM1602_IIC1.SDA
  N21: Part1.A5/SCL, LCM1602_IIC1.SCL
  N22: Part1.D2, S1.Pin_1, S1.Pin_2
  N23: Part1.D3_PWM, S2.Pin_1, S2.Pin_2
  N24: Part1.RESET, RESET.Pin_1, RESET.Pin_2
  N25: Part1.VIN, V2.V+
  N26: DC_FAN.pin_1, V3.V-
  N27: DC_FAN.pin_2, V3.V+
  VSS: LCD1.VSS, LCM1602_IIC1.VSS
  VDD: LCD1.VDD, LCM1602_IIC1.VDD
  N28: LCD1.V0, LCM1602_IIC1.V0
  N29: LCD1.RS, LCM1602_IIC1.RS
  N30: LCD1.R/W, LCM1602_IIC1.RW
  N31: LCD1.E, LCM1602_IIC1.E
  N32: LCD1.DB0, LCM1602_IIC1.D0
  N33: LCD1.DB1, LCM1602_IIC1.D1
  N34: LCD1.DB2, LCM1602_IIC1.D2
  N35: LCD1.DB3, LCM1602_IIC1.D3
  N36: LCD1.DB4, LCM1602_IIC1.D4
  N37: LCD1.DB5, LCM1602_IIC1.D5
  N38: LCD1.DB6, LCM1602_IIC1.D6
  N39: LCD1.DB7, LCM1602_IIC1.D7
  N40: LCD1.LED+, LCM1602_IIC1.A
  N41: LCD1.LED-, LCM1602_IIC1.K
  N42: LCM1602_IIC1.LED_A, LCM1602_IIC1.LED_B

notes:
  power supply 12v
  LOADCELL

custom parts:
  LCM1602 IIC: I2C-Module to use a 1602 or 2004 LCD on with the wire.h libory Serial LCD Modul
